# Fritzing sketch 01_LED (saved by Fritzing 0.9.3b)
breadboards: 1

parts:
  Bauteil1 = Arduino Nano (Rev3.0)
  LED1 = LED - 5mm [color="Red (633nm)" package="5 mm [THT]"]
  R1 = Resistor [tolerance=±5% resistance=330 package=THT]

nets:
  N1: Bauteil1.GND, LED1.cathode
  N2: Bauteil1.D13/SCK, R1.Pin_1
  N3: LED1.anode, R1.Pin_0
