# Fritzing sketch 03_LED_dimmer (saved by Fritzing 0.9.3b)
breadboards: 1

parts:
  Bauteil1 = Arduino Nano (Rev3.0)
  R1 = Trimmer Potentiometer [maximum_resistance=10kΩ package=THT]
  LED1 = LED - 5mm [color="Red (633nm)" package="5 mm [THT]"]
  R2 = Resistor [tolerance=±5% resistance=220 package=THT]

nets:
  N1: Bauteil1.GND, R1.leg2, R2.Pin_1
  N2: Bauteil1.D9, LED1.anode
  N3: Bauteil1.5V, R1.leg1
  N4: Bauteil1.A0, R1.wiper
  N5: LED1.cathode, R2.Pin_0
