# Fritzing sketch 10_Taster_PullDown (saved by Fritzing 0.9.3b)
breadboards: 1

parts:
  Bauteil1 = Arduino Nano (Rev3.0)
  S1 = Pushbutton [package="[THT]"]
  R1 = Resistor [tolerance=±5% resistance=10k package=THT]

nets:
  N1: Bauteil1.GND, S1.Pin_1, S1.Pin_2, R1.Pin_0
  N2: Bauteil1.D7, S1.Pin_3, S1.Pin_4, R1.Pin_1
