# Fritzing sketch 12_Taster_PullUp_LED (saved by Fritzing 0.9.3b)
breadboards: 1

parts:
  Bauteil1 = Arduino Nano (Rev3.0)
  S1 = Pushbutton [package="[THT]"]
  R1 = Resistor [tolerance=±5% resistance=10k package=THT]
  LED1 = LED - 5mm [color="Red (633nm)" package="5 mm [THT]"]
  R2 = Resistor [tolerance=±5% resistance=330 package=THT]

nets:
  N1: Bauteil1.GND, S1.Pin_1, S1.Pin_2, R2.Pin_1
  N2: Bauteil1.D8, S1.Pin_3, S1.Pin_4, R1.Pin_1
  N3: Bauteil1.5V, R1.Pin_0
  N4: Bauteil1.D13/SCK, LED1.anode
  N5: LED1.cathode, R2.Pin_0
