# Fritzing sketch 14_Theremin (saved by Fritzing 0.9.3b)
breadboards: 1

parts:
  Bauteil1 = Arduino Nano (Rev3.0)
  R1 = Resistor [tolerance=±5% resistance=10k package=THT]
  R2 = Photocell (LDR) [package=THT]
  J1 = Piezo Speaker

nets:
  N1: Bauteil1.GND, R1.Pin_0, J1.pin1
  N2: Bauteil1.D12/MISO, J1.pin2
  N3: Bauteil1.5V, R2.pin_1
  N4: R1.Pin_1, R2.pin_0
