# Fritzing sketch 15_PCF8574 (saved by Fritzing 0.9.3b)
breadboards: 1

parts:
  Bauteil1 = Arduino Nano (Rev3.0)
  IC1 = IC, DIP package, 16 pins [chip_label=IC]
  LED1 = LED - 5mm [color="Red (633nm)" package="5 mm [THT]"]
  LED2 = LED - 5mm [color="Red (633nm)" package="5 mm [THT]"]
  LED3 = LED - 5mm [color="Red (633nm)" package="5 mm [THT]"]
  LED4 = LED - 5mm [color="Red (633nm)" package="5 mm [THT]"]
  LED5 = LED - 5mm [color="Red (633nm)" package="5 mm [THT]"]
  LED6 = LED - 5mm [color="Red (633nm)" package="5 mm [THT]"]
  LED7 = LED - 5mm [color="Red (633nm)" package="5 mm [THT]"]
  LED8 = LED - 5mm [color="Red (633nm)" package="5 mm [THT]"]
  R1 = Resistor [tolerance=±5% resistance=330 package=THT]
  R2 = Resistor [tolerance=±5% resistance=330 package=THT]
  R3 = Resistor [tolerance=±5% resistance=330 package=THT]
  R4 = Resistor [tolerance=±5% resistance=330 package=THT]
  R5 = Resistor [tolerance=±5% resistance=330 package=THT]
  R6 = Resistor [tolerance=±5% resistance=330 package=THT]
  R7 = Resistor [tolerance=±5% resistance=330 package=THT]
  R8 = Resistor [tolerance=±5% resistance=330 package=THT]

nets:
  N1: Bauteil1.GND, IC1.pin1, IC1.pin2, IC1.pin3, IC1.pin8
  N2: Bauteil1.5V, IC1.pin16, R1.Pin_1, R3.Pin_1, R4.Pin_1, R5.Pin_1, R6.Pin_1, R7.Pin_1, R8.Pin_1
  N3: Bauteil1.A5, IC1.pin15
  N4: Bauteil1.A4, IC1.pin14
  N5: IC1.pin4, LED4.cathode
  N6: IC1.pin5, LED3.cathode
  N7: IC1.pin6, LED2.cathode
  N8: IC1.pin7, LED1.cathode
  N9: IC1.pin9, LED8.cathode
  N10: IC1.pin10, LED5.cathode
  N11: IC1.pin11, LED6.cathode
  N12: IC1.pin12, LED7.cathode
  N13: LED1.anode, R1.Pin_0
  N14: LED2.anode, R2.Pin_0
  N15: LED3.anode, R3.Pin_0
  N16: LED4.anode, R4.Pin_0
  N17: LED5.anode, R5.Pin_0
  N18: LED6.anode, R6.Pin_0
  N19: LED7.anode, R7.Pin_0
  N20: LED8.anode, R8.Pin_0
