# Fritzing sketch 16_ShiftRegister (saved by Fritzing 0.9.4)
circuit board: 8.46667cm x 5.64444cm
breadboards: 1

parts:
  Bauteil1 = Arduino Nano (Rev3.0)
  U1 = 74HC595 [package="DIP16 [THT]"]
  R1 = Resistor [tolerance=±5% resistance=330 package=THT]
  R2 = Resistor [tolerance=±5% resistance=330 package=THT]
  R3 = Resistor [tolerance=±5% resistance=330 package=THT]
  R4 = Resistor [tolerance=±5% resistance=330 package=THT]
  R5 = Resistor [tolerance=±5% resistance=330 package=THT]
  R6 = Resistor [tolerance=±5% resistance=330 package=THT]
  R7 = Resistor [tolerance=±5% resistance=330 package=THT]
  R8 = Resistor [tolerance=±5% resistance=330 package=THT]
  DI1 = 7-Segment LED Display [package=THT]

nets:
  GND: Bauteil1.GND, U1.GND, U1.OE, DI1.commAnode#2
  N1: Bauteil1.D2, U1.SH_CP
  N2: Bauteil1.D3, U1.ST_CP
  N3: Bauteil1.D4, U1.DS
  5V: Bauteil1.5V, U1.MR, U1.VCC
  N4: U1.Q1, R7.Pin_0
  N5: U1.Q2, R4.Pin_0
  N6: U1.Q3, R3.Pin_1
  N7: U1.Q4, R1.Pin_1
  N8: U1.Q5, R6.Pin_1
  N9: U1.Q6, R2.Pin_1
  N10: U1.Q7, R5.Pin_0
  N11: U1.Q0, R8.Pin_0
  N12: R1.Pin_0, DI1.cathodeE
  N13: R2.Pin_0, DI1.cathodeG
  N14: R3.Pin_0, DI1.cathodeD
  N15: R4.Pin_1, DI1.cathodeC
  N16: R5.Pin_1, DI1.cathodeDP
  N17: R6.Pin_0, DI1.cathodeF
  N18: R7.Pin_1, DI1.cathodeB
  N19: R8.Pin_1, DI1.cathodeA
