# Fritzing sketch 20_BMP280 (saved by Fritzing 0.9.3b)
breadboards: 1

parts:
  Bauteil1 = Barometric Pressure Sensor - BMP085 Breakout
  Bauteil2 = Arduino Nano (Rev3.0)

nets:
  N1: Bauteil1.EOC, Bauteil2.A4
  N2: Bauteil1.XCLR, Bauteil2.A5
  N3: Bauteil1.SCL, Bauteil2.GND
  N4: Bauteil1.SDA, Bauteil2.3V3
