# Fritzing sketch 26_UI_characteristic (saved by Fritzing 0.9.3b)
breadboards: 1

parts:
  R1 = Resistor [tolerance=±5% resistance=100 package=THT]
  R2 = Resistor [tolerance=±5% resistance=100 package=THT]
  R3 = Resistor [tolerance=±5% resistance=100 package=THT]
  LED1 = LED - 5mm [color="Red (633nm)" package="5 mm [THT]"]
  Nano = Arduino Nano (Rev3.0)
  C1 = Electrolytic Capacitor [capacitance=10µF voltage=10V package="100 mil [THT, electrolytic]"]

nets:
  N1: R1.Pin_0, R2.Pin_0, R3.Pin_0, Nano.A0, C1.+
  N2: R1.Pin_1, Nano.D11/MOSI
  N3: R2.Pin_1, Nano.D3
  N4: R3.Pin_1, LED1.anode, Nano.A1
  N5: LED1.cathode, Nano.GND, C1.-
