# Fritzing sketch 27_trafficlight (saved by Fritzing 0.9.3b)
breadboards: 1

parts:
  Bauteil1 = Arduino Nano (Rev3.0)
  S1 = Pushbutton [package="[THT]"]
  R1 = Resistor [tolerance=±5% resistance=330 package=THT]
  R2 = Resistor [tolerance=±5% resistance=330 package=THT]
  R3 = Resistor [tolerance=±5% resistance=330 package=THT]
  LED1 = LED - 5mm [color="Red (633nm)" package="5 mm [THT]"]
  LED2 = LED - 5mm [color="Yellow (595nm)" package="5 mm [THT]"]
  LED3 = LED - 5mm [color="Green (570nm)" package="5 mm [THT]"]

nets:
  N1: Bauteil1.GND, S1.Pin_1, S1.Pin_2, R1.Pin_1, R2.Pin_1, R3.Pin_1
  N2: Bauteil1.D2, LED1.anode
  N3: Bauteil1.D3, LED2.anode
  N4: Bauteil1.D4, LED3.anode
  N5: Bauteil1.D5, S1.Pin_3, S1.Pin_4
  N6: R1.Pin_0, LED1.cathode
  N7: R2.Pin_0, LED3.cathode
  N8: R3.Pin_0, LED2.cathode
