# Fritzing sketch 33_melody (saved by Fritzing 0.9.3b)
breadboards: 1

parts:
  Bauteil1 = Arduino Nano (Rev3.0)
  J1 = Piezo Speaker
  R1 = Resistor [tolerance=±5% resistance=330 package=THT]

nets:
  N1: Bauteil1.GND, R1.Pin_1
  N2: Bauteil1.D10, J1.pin2
  N3: J1.pin1, R1.Pin_0
