# Fritzing sketch 35_BMP280_PCF8574_LCD (saved by Fritzing 0.9.4)
breadboards: 1

parts:
  Bauteil1 = LCD1602-I2C
  Bauteil2 = Arduino Nano (Rev3.0) (ICSP)
  Bauteil3 = GY-BMEP280 Barometric Pressure Sensor - Breakout

nets:
  GND: Bauteil1.GND, Bauteil2.GND, Bauteil3.GND
  VCC: Bauteil1.VCC, Bauteil2.VIN
  N1: Bauteil1.SDA, Bauteil2.A4, Bauteil3.SDA
  N2: Bauteil1.SCL, Bauteil2.A5, Bauteil3.SCL
  3V3: Bauteil2.3V3, Bauteil3.VCC

custom parts:
  LCD1602-I2C: A standard character display, usually with 2x16 characters. Comes in many colors with LCM1602 IIC attached.
  GY-BMEP280 Barometric Pressure Sensor - Breakout: The BME280 is a chip which was originally designed for the next generation of smartphones. It is made up of a very accurate pressure sensor and an associated temperature sensor which helps calibrate the pressure readings. And just for fun they threw in a pretty solid humidity sensor in there as well! So with an I2C connection you have access to enough weather data to make some pretty good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
