# Fritzing sketch 36_PCF8574_LCD (saved by Fritzing 0.9.4)
breadboards: 1

parts:
  Bauteil1 = LCD1602-I2C
  Bauteil2 = Arduino Nano (Rev3.0) (ICSP)

nets:
  GND: Bauteil1.GND, Bauteil2.GND
  VCC: Bauteil1.VCC, Bauteil2.VIN
  N1: Bauteil1.SDA, Bauteil2.A4
  N2: Bauteil1.SCL, Bauteil2.A5

custom parts:
  LCD1602-I2C: A standard character display, usually with 2x16 characters. Comes in many colors with LCM1602 IIC attached.
