# Fritzing sketch 37_CD4026_Steckbrett_7-Segment (saved by Fritzing 0.9.6b)
breadboards: 1

parts:
  Part1 = Arduino Nano (Rev3.0) (ICSP)
  DI1 = 7 Segment Display
  IC1 = IC, DIP package, 16 pins [chip_label=CD4026]

nets:
  N1: Part1.D1/TX, DI1.Segment_G, IC1.pin7
  N2: Part1.D8, IC1.pin15
  N3: Part1.GND, Part1.D13/SCK
  N4: Part1.AREF, DI1.Segment_C, IC1.pin13
  N5: DI1.Segment_E, IC1.pin11
  N6: DI1.Segment_D, IC1.pin9
  N7: DI1.common_cathode, IC1.pin8
  N8: DI1.Segment_B, IC1.pin12
  N9: DI1.Segment_A, IC1.pin10
  N10: DI1.Segment_F, IC1.pin6
  N11: IC1.pin3, IC1.pin16
