# Fritzing sketch 02_potentiometer (saved by Fritzing 0.9.3b)
breadboards: 1

parts:
  Bauteil1 = Arduino Nano (Rev3.0)
  R1 = Trimmer Potentiometer [maximum_resistance=10kΩ package=THT]

nets:
  N1: Bauteil1.GND, R1.leg2
  N2: Bauteil1.5V, R1.leg1
  N3: Bauteil1.A0, R1.wiper
