# Fritzing sketch 04_spannungsteiler (saved by Fritzing 0.9.3b)
breadboards: 1

parts:
  Bauteil1 = Arduino Nano (Rev3.0)
  R1 = Resistor [tolerance=±5% resistance=2.2k package=THT]
  R2 = Resistor [tolerance=±5% resistance=3.3k package=THT]

nets:
  N1: Bauteil1.GND, R2.Pin_1
  N2: Bauteil1.5V, R1.Pin_0
  N3: Bauteil1.A0, R1.Pin_1, R2.Pin_0
