# Fritzing sketch 06b_Dämmerungsschalter_mit_Poti (saved by Fritzing 0.9.3b)
breadboards: 1

parts:
  Bauteil1 = Arduino Nano (Rev3.0)
  R1 = Trimmer Potentiometer [maximum_resistance=10kΩ package=THT]
  LED1 = LED - 5mm [color="Red (633nm)" package="5 mm [THT]"]
  R2 = Resistor [tolerance=±5% resistance=330 package=THT]
  R5 = Photocell (LDR) [package=THT]
  R3 = Resistor [tolerance=±5% resistance=10k package=THT]

nets:
  N1: Bauteil1.GND, R1.leg2, R2.Pin_1, R3.Pin_0
  N2: Bauteil1.D9, LED1.anode
  N3: Bauteil1.5V, R1.leg1, R5.pin_1
  N4: Bauteil1.A1, R5.pin_0, R3.Pin_1
  N5: Bauteil1.A0, R1.wiper
  N6: LED1.cathode, R2.Pin_0
