# Fritzing sketch 07_Dämmerungsschalter_ohne_µC (saved by Fritzing 0.9.3b)
breadboards: 1

parts:
  R1 = Resistor [tolerance=±5% resistance=220 package=THT]
  R2 = Resistor [tolerance=±5% resistance=470 package=THT]
  R3 = Resistor [tolerance=±5% resistance=470 package=THT]
  R4 = Resistor [tolerance=±5% resistance=470 package=THT]
  Q1 = PNP-Transistor [package="TO92 [THT]"]
  LED1 = LED - 5mm [color="Red (633nm)" package="5 mm [THT]"]
  R5 = Photocell (LDR) [package=THT]

nets:
  N1: R1.Pin_0, LED1.cathode
  N2: R1.Pin_1, R3.Pin_1, R4.Pin_1, R5.pin_0
  N3: R2.Pin_0, Q1.B
  N4: R2.Pin_1, R3.Pin_0, R4.Pin_0, R5.pin_1
  N5: Q1.C, LED1.anode
