# Fritzing sketch 08_Transistorschaltung (saved by Fritzing 0.9.3b)
breadboards: 1

parts:
  Bauteil1 = Arduino Nano (Rev3.0)
  Q1 = PNP-Transistor [package="TO92 [THT]"]
  LED1 = LED - 5mm [color="Red (633nm)" package="5 mm [THT]"]
  R1 = Resistor [tolerance=±5% resistance=330 package=THT]
  R2 = Resistor [tolerance=±5% resistance=1k package=THT]

nets:
  N1: Bauteil1.GND, R1.Pin_0
  N2: Bauteil1.5V, Q1.E
  N3: Bauteil1.D13/SCK, R2.Pin_0
  N4: Q1.C, LED1.anode
  N5: LED1.cathode, R1.Pin_1
