# Fritzing sketch 17_BMP280_16x2_LCD (saved by Fritzing 0.9.3b)
breadboards: 1

parts:
  Bauteil2 = Barometric Pressure Sensor - BMP085 Breakout
  Bauteil3 = Arduino Nano (Rev3.0)
  Bauteil4 = LCD1602-I2C

nets:
  N1: Bauteil2.EOC, Bauteil3.A4, Bauteil4.SDA
  N2: Bauteil2.XCLR, Bauteil3.A5, Bauteil4.SCL
  GND: Bauteil2.SCL, Bauteil3.GND, Bauteil4.GND
  N3: Bauteil2.SDA, Bauteil3.3V3
  5V: Bauteil3.5V, Bauteil4.VCC

custom parts:
  LCD1602-I2C: A standard character display, usually with 2x16 characters. Comes in many colors with LCM1602 IIC attached.
