# Fritzing sketch 18_DHT11 (saved by Fritzing 0.9.3b)
breadboards: 1

parts:
  Bauteil1 = Arduino Nano (Rev3.0)
  DHT1 = DHT22 Humidity and Temperature Sensor
  R1 = Resistor [tolerance=±5% resistance=10k package=THT]

nets:
  GND: Bauteil1.GND, DHT1.GND
  N1: Bauteil1.D4, DHT1.DATA, R1.Pin_0
  5V: Bauteil1.5V, DHT1.VDD, R1.Pin_1
